# Fritzing sketch RC_car_회로도_4(3Sensor_Pattern) (saved by Fritzing 1.0.4)
breadboards: 1

parts:
  부품1 = Arduino Uno (Rev3)
  Mod1 = Amica NodeMCU DEVKIT 1.0
  M1 = DC Motor [voltage_(max)=6V voltage_(min)=3V]
  M2 = DC Motor [voltage_(max)=6V voltage_(min)=3V]
  R1 = Resistor [tolerance=±5% power=0.25W resistance=220 package=THT]
  R2 = Resistor [tolerance=±5% power=0.25W resistance=220 package=THT]
  R3 = Resistor [tolerance=±5% power=0.25W resistance=220 package=THT]
  U1 = L9110 H-bridge module [part_number="L9110 H-bridge"]
  Enc1 = shaft encoder
  Enc2 = shaft encoder
  M3 = RioRand LM2596
  VCC1 = Battery [internal_resistance=0.1Ω]
  M4 = fc-51 [package=THT]
  M5 = fc-51 [package=THT]
  M6 = fc-51 [package=THT]

nets:
  N1: 부품1.A0, M5.pin1
  N2: 부품1.A1, M4.pin1
  N3: 부품1.A2, M6.pin1
  N4: 부품1.D9_PWM, U1.A-IA
  N5: 부품1.D10_PWM/SS, U1.A-IB
  N6: 부품1.D0/RX, Mod1.pin3
  N7: 부품1.D1/TX, R1.Pin_1, R2.Pin_0, R3.Pin_0
  N8: 부품1.D2, Enc1.OUT
  N9: 부품1.D3_PWM, Enc2.OUT
  N10: 부품1.D5_PWM, U1.B-IB
  N11: 부품1.D6_PWM, U1.B-IA
  GND: 부품1.GND, Mod1.pin2, Mod1.pin_25, Mod1.pin_29, R1.Pin_0, U1.GND, Enc1.GND, Enc2.GND, M3.Pin_2, M3.Pin_4, VCC1.-, M4.pin2, M5.pin2
  VCC: 부품1.VIN, Mod1.pin_30, Enc1.VCC, Enc2.VCC, M3.Pin_3, M4.pin3, M5.pin3, M6.pin3
  N12: Mod1.pin4, R2.Pin_1, R3.Pin_1
  N13: M1.pin_1, U1.MOTOR_B-A
  N14: M1.pin_2, U1.MOTOR_B-B
  N15: M2.pin_1, U1.MOTOR_A-B
  N16: M2.pin_2, U1.MOTOR_A-A
  N17: U1.VCC, M3.Pin_1, VCC1.+
