# Fritzing sketch RC_car_회로도 (saved by Fritzing 1.0.4)
breadboards: 1

parts:
  부품1 = Arduino Uno (Rev3)
  Mod1 = Amica NodeMCU DEVKIT 1.0
  VCC1 = 4 x AAA Battery Mount [internal_resistance=0.1Ω]
  VCC2 = Battery block 9V [internal_resistance=0.1Ω]
  M1 = DC Motor [voltage_(max)=6V voltage_(min)=3V]
  M2 = DC Motor [voltage_(max)=6V voltage_(min)=3V]
  R1 = Resistor [tolerance=±5% power=0.25W resistance=220 package=THT]
  R2 = Resistor [tolerance=±5% power=0.25W resistance=220 package=THT]
  R3 = Resistor [tolerance=±5% power=0.25W resistance=220 package=THT]
  U1 = L9110 H-bridge module [part_number="L9110 H-bridge"]
  Enc1 = shaft encoder
  Enc2 = shaft encoder

nets:
  N1: 부품1.D9_PWM, U1.A-IA
  N2: 부품1.D10_PWM/SS, U1.A-IB
  N3: 부품1.D0/RX, Mod1.pin3
  N4: 부품1.D1/TX, R1.Pin_1, R2.Pin_0, R3.Pin_0
  N5: 부품1.D2, Enc1.OUT
  N6: 부품1.D3_PWM, Enc2.OUT
  N7: 부품1.D5_PWM, U1.B-IB
  N8: 부품1.D6_PWM, U1.B-IA
  VCC: 부품1.5V, Mod1.pin_30, Enc1.VCC, Enc2.VCC
  GND: 부품1.GND, Mod1.pin2, Mod1.pin_25, VCC1.-, VCC2.-, R1.Pin_0, U1.GND, Enc1.GND, Enc2.GND
  N9: 부품1.VIN, VCC1.+
  N10: Mod1.pin4, R2.Pin_1, R3.Pin_1
  N11: VCC2.+, U1.VCC
  N12: M1.pin_1, U1.MOTOR_B-A
  N13: M1.pin_2, U1.MOTOR_B-B
  N14: M2.pin_1, U1.MOTOR_A-B
  N15: M2.pin_2, U1.MOTOR_A-A
